// Logisim project riscv_single_cycle.circ as structural Verilog: 18 circuits, main circuit main
module main (
);

  wire branch_1_output, button_1_out, clock_1_out, control_1_mem_2_reg, control_1_op_b_selector,
       control_1_reg_write, control_1_store;
  wire [1:0] control_1_imm_selector, control_1_next_pc, control_1_op_a_selector;
  wire [2:0] rom_1_data_2;
  wire [3:0] control_1_selector;
  wire [31:0] adder_1_out, adder_2_out, alu_main_1_out_4, imm_generation_1_i, imm_generation_1_s,
       imm_generation_1_sb, imm_generation_1_u, imm_generation_1_uj, multiplexer_1_out, multiplexer_2_out,
       multiplexer_3_out, multiplexer_4_out, multiplexer_5_out, multiplexer_6_out, ram_1_data, register_1_q,
       resistor_1_rs1, resistor_1_rs2, rom_1_data;

  Clock clock_1 (.out(clock_1_out));
  Button button_1 (.out(button_1_out));
  IMM_GENERATION imm_generation_1 (
    .I(imm_generation_1_i), .S(imm_generation_1_s), .SB(imm_generation_1_sb), .U(imm_generation_1_u),
    .UJ(imm_generation_1_uj), .PC(register_1_q), .INS({rom_1_data[31:15], rom_1_data_2, rom_1_data[11:0]}));
  Multiplexer #(.select(2), .width(32), .enable("false")) multiplexer_1 (
    .in0(adder_1_out), .in1(imm_generation_1_uj), .in2(adder_2_out), .in3(multiplexer_3_out),
    .out(multiplexer_1_out), .sel(control_1_next_pc));
  Register #(.width(32)) register_1 (
    .D(multiplexer_1_out), .Q(register_1_q), .clk(clock_1_out), .clr(button_1_out));  // open: en
  Adder #(.width(32)) adder_1 (.a(register_1_q), .b(32'h4), .out(adder_1_out));  // open: cin, cout
  Multiplexer #(.select(2), .width(32), .enable("false")) multiplexer_2 (
    .in0(imm_generation_1_i), .in1(imm_generation_1_s), .in2(imm_generation_1_u), .out(multiplexer_2_out),
    .sel(control_1_imm_selector));  // open: in3
  Multiplexer #(.width(32), .enable("false")) multiplexer_3 (
    .in0(adder_1_out), .in1(imm_generation_1_sb), .out(multiplexer_3_out), .sel(branch_1_output));
  BRANCH branch_1 (.\output (branch_1_output), .RS_1(resistor_1_rs1), .RS_2(resistor_1_rs2), .selector(rom_1_data_2));
  ROM #(.addrWidth(12), .dataWidth(32)) rom_1 (
    .addr(register_1_q[13:2]), .data({rom_1_data[31:15], rom_1_data_2, rom_1_data[11:0]}));  // open: sel
  RESISTOR resistor_1 (
    .RS1(resistor_1_rs1), .RS2(resistor_1_rs2), .data_In(multiplexer_6_out), .enable(control_1_reg_write),
    .RD(rom_1_data[11:7]), .in_6(clock_1_out), .M1_selector(rom_1_data[19:15]),
    .M2_selector(rom_1_data[24:20]));
  CONTROL control_1 (
    .opcode_7_bit(rom_1_data[6:0]), .reg_write(control_1_reg_write), .store(control_1_store),
    .mem_2_reg(control_1_mem_2_reg), .op_a_selector(control_1_op_a_selector),
    .op_b_selector(control_1_op_b_selector), .imm_selector(control_1_imm_selector),
    .next_pc(control_1_next_pc), .fun_3_bit(rom_1_data_2), .fun_7_bit(rom_1_data[30]),
    .selector(control_1_selector));  // open: branch, alu
  Multiplexer #(.select(2), .width(32), .enable("false")) multiplexer_4 (
    .in0(resistor_1_rs1), .in1(adder_1_out), .in2(register_1_q), .in3({32{1'b0}}), .out(multiplexer_4_out),
    .sel(control_1_op_a_selector));
  Multiplexer #(.width(32), .enable("false")) multiplexer_5 (
    .in0(resistor_1_rs2), .in1(multiplexer_2_out), .out(multiplexer_5_out), .sel(control_1_op_b_selector));
  Adder #(.width(32)) adder_2 (.a(imm_generation_1_i), .b(resistor_1_rs1), .out(adder_2_out));  // open: cin, cout
  alu_main alu_main_1 (
    .in_3(control_1_selector), .out_4(alu_main_1_out_4), .in_1(multiplexer_4_out), .in_2(multiplexer_5_out));
  RAM #(.addrWidth(12), .dataWidth(32), .bus("separate")) ram_1 (
    .addr(alu_main_1_out_4[13:2]), .din(resistor_1_rs2), .data(ram_1_data), .str(control_1_store),
    .clk(clock_1_out), .ld(control_1_mem_2_reg), .clr(button_1_out));  // open: sel
  Multiplexer #(.width(32), .enable("false")) multiplexer_6 (
    .in0(alu_main_1_out_4), .in1(ram_1_data), .out(multiplexer_6_out), .sel(control_1_mem_2_reg));

  // Notes on the sheet:
  //   RV32I  SINGLE CYCLE 
  //   MADE BY ZAIN ALI
endmodule

// TYPE DECODE
module decoder (
  input  [6:0] in_1,
  output R,
  output I,
  output I__LOAD,
  output I__JALR,
  output S,
  output SB,
  output U__AUIPC,
  output U__LUI,
  output UJ__JAL
);

  wire comparator_2_lt;

  Comparator #(.width(7)) comparator_1 (.a(in_1), .b(7'b0110011), .eq(R));  // open: gt, lt
  Comparator #(.width(7)) comparator_2 (.a(in_1), .b(7'b0010011), .eq(I), .lt(comparator_2_lt));  // open: gt
  Comparator #(.width(7)) comparator_3 (.a(in_1), .b(7'b0100011), .eq(S));  // open: gt, lt
  Comparator #(.width(7)) comparator_4 (.a(in_1), .b(7'b1100011), .eq(SB));  // open: gt, lt
  Comparator #(.width(7)) comparator_5 (.a(in_1), .b(7'b0010111), .eq(U__AUIPC));  // open: gt, lt
  Comparator #(.width(7)) comparator_6 (.a(in_1), .b(7'b1101111), .eq(UJ__JAL));  // open: gt, lt
  Comparator #(.width(7)) comparator_7 (.a(in_1), .b(7'b0000011), .eq(I__LOAD));  // open: gt, lt
  Comparator #(.width(7)) comparator_8 (.a(in_1), .b(7'b0110111), .eq(U__LUI));  // open: gt, lt
  Comparator #(.width(7)) comparator_9 (.a(in_1), .b(7'b1100111), .eq(I__JALR));  // open: gt, lt

  // Notes on the sheet:
  //   R-type
  //   I -type
  //   S-type
  //   SB - type
  //   U -t ype
  //   UJ - type
endmodule

module IMM_GENERATION (
  input  [31:0] PC,
  input  [31:0] INS,
  output [31:0] I,
  output [31:0] S,
  output [31:0] SB,
  output [31:0] U,
  output [31:0] UJ
);

  wire [31:0] bit_extender_1_out, bit_extender_4_out, bit_extender_5_out;

  assign bit_extender_1_out = {{12{1'b0}}, INS[31:12]};  // Bit_Extender bit_extender_1
  assign I = {{20{INS[31]}}, INS[31:20]};  // Bit_Extender bit_extender_2
  assign S = {{20{INS[31]}}, {INS[31:25], INS[11:7]}};  // Bit_Extender bit_extender_3
  assign bit_extender_4_out = {{19{INS[31]}}, {INS[31], INS[7], INS[30:25], INS[11:8], 1'b0}};  // Bit_Extender bit_extender_4
  assign bit_extender_5_out = {{11{INS[31]}}, {INS[31], INS[19:12], INS[20], INS[30:21], 1'b0}};  // Bit_Extender bit_extender_5
  Adder #(.width(32)) adder_1 (.a(bit_extender_4_out), .b(PC), .out(SB));  // open: cin, cout
  Shifter #(.width(32)) shifter_1 (.in(bit_extender_1_out), .\dist (5'b01100), .out(U));
  Adder #(.width(32)) adder_2 (.a(bit_extender_5_out), .b(PC), .out(UJ));  // open: cin, cout
endmodule

module RESISTOR (
  input  [31:0] data_In,
  input  enable,
  input  [4:0] M1_selector,
  input  [4:0] RD,
  input  [4:0] M2_selector,
  input  in_6,
  output [31:0] RS1,
  output [31:0] RS2
);

  wire decoder_1_out1, decoder_1_out2, decoder_1_out3, decoder_1_out4, decoder_1_out5, decoder_1_out6,
       decoder_1_out7, decoder_1_out8, decoder_1_out9, decoder_1_out10, decoder_1_out11, decoder_1_out12,
       decoder_1_out13, decoder_1_out14, decoder_1_out15, decoder_1_out16, decoder_1_out17, decoder_1_out18,
       decoder_1_out19, decoder_1_out20, decoder_1_out21, decoder_1_out22, decoder_1_out23, decoder_1_out24,
       decoder_1_out25, decoder_1_out26, decoder_1_out27, decoder_1_out28, decoder_1_out29, decoder_1_out30,
       decoder_1_out31;
  wire [31:0] register_1_q, register_2_q, register_3_q, register_4_q, register_5_q, register_6_q,
       register_7_q, register_8_q, register_9_q, register_10_q, register_11_q, register_12_q, register_13_q,
       register_14_q, register_15_q, register_16_q, register_17_q, register_18_q, register_19_q,
       register_20_q, register_21_q, register_22_q, register_23_q, register_24_q, register_25_q,
       register_26_q, register_27_q, register_28_q, register_29_q, register_30_q, register_31_q;

  Decoder #(.select(5), .disabled(0)) decoder_1 (
    .out1(decoder_1_out1), .out2(decoder_1_out2), .out3(decoder_1_out3), .out4(decoder_1_out4),
    .out5(decoder_1_out5), .out6(decoder_1_out6), .out7(decoder_1_out7), .out8(decoder_1_out8),
    .out9(decoder_1_out9), .out10(decoder_1_out10), .out11(decoder_1_out11), .out12(decoder_1_out12),
    .out13(decoder_1_out13), .out14(decoder_1_out14), .out15(decoder_1_out15), .out16(decoder_1_out16),
    .out17(decoder_1_out17), .out18(decoder_1_out18), .out19(decoder_1_out19), .out20(decoder_1_out20),
    .out21(decoder_1_out21), .out22(decoder_1_out22), .out23(decoder_1_out23), .out24(decoder_1_out24),
    .out25(decoder_1_out25), .out26(decoder_1_out26), .out27(decoder_1_out27), .out28(decoder_1_out28),
    .out29(decoder_1_out29), .out30(decoder_1_out30), .out31(decoder_1_out31), .sel(RD), .en(enable));  // open: out0
  Register #(.width(32)) register_1 (.D(data_In), .en(decoder_1_out1), .Q(register_1_q), .clk(in_6));  // open: clr
  Register #(.width(32)) register_2 (.D(data_In), .en(decoder_1_out2), .Q(register_2_q), .clk(in_6));  // open: clr
  Register #(.width(32)) register_3 (.D(data_In), .en(decoder_1_out3), .Q(register_3_q), .clk(in_6));  // open: clr
  Register #(.width(32)) register_4 (.D(data_In), .en(decoder_1_out4), .Q(register_4_q), .clk(in_6));  // open: clr
  Register #(.width(32)) register_5 (.D(data_In), .en(decoder_1_out5), .Q(register_5_q), .clk(in_6));  // open: clr
  Bit_Extender #(.in_width(20), .out_width(32), .\type ("sign")) bit_extender_1 ();  // open: in, out
  Register #(.width(32)) register_6 (.D(data_In), .en(decoder_1_out6), .Q(register_6_q), .clk(in_6));  // open: clr
  Register #(.width(32)) register_7 (.D(data_In), .en(decoder_1_out7), .Q(register_7_q), .clk(in_6));  // open: clr
  Register #(.width(32)) register_8 (.D(data_In), .en(decoder_1_out8), .Q(register_8_q), .clk(in_6));  // open: clr
  Register #(.width(32)) register_9 (.D(data_In), .en(decoder_1_out9), .Q(register_9_q), .clk(in_6));  // open: clr
  Register #(.width(32)) register_10 (.D(data_In), .en(decoder_1_out10), .Q(register_10_q), .clk(in_6));  // open: clr
  Register #(.width(32)) register_11 (.D(data_In), .en(decoder_1_out11), .Q(register_11_q), .clk(in_6));  // open: clr
  Register #(.width(32)) register_12 (.D(data_In), .en(decoder_1_out12), .Q(register_12_q), .clk(in_6));  // open: clr
  Register #(.width(32)) register_13 (.D(data_In), .en(decoder_1_out13), .Q(register_13_q), .clk(in_6));  // open: clr
  Register #(.width(32)) register_14 (.D(data_In), .en(decoder_1_out14), .Q(register_14_q), .clk(in_6));  // open: clr
  Register #(.width(32)) register_15 (.D(data_In), .en(decoder_1_out15), .Q(register_15_q), .clk(in_6));  // open: clr
  Register #(.width(32)) register_16 (.D(data_In), .en(decoder_1_out16), .Q(register_16_q), .clk(in_6));  // open: clr
  Register #(.width(32)) register_17 (.D(data_In), .en(decoder_1_out17), .Q(register_17_q), .clk(in_6));  // open: clr
  Register #(.width(32)) register_18 (.D(data_In), .en(decoder_1_out18), .Q(register_18_q), .clk(in_6));  // open: clr
  Register #(.width(32)) register_19 (.D(data_In), .en(decoder_1_out19), .Q(register_19_q), .clk(in_6));  // open: clr
  Register #(.width(32)) register_20 (.D(data_In), .en(decoder_1_out20), .Q(register_20_q), .clk(in_6));  // open: clr
  Register #(.width(32)) register_21 (.D(data_In), .en(decoder_1_out21), .Q(register_21_q), .clk(in_6));  // open: clr
  Register #(.width(32)) register_22 (.D(data_In), .en(decoder_1_out22), .Q(register_22_q), .clk(in_6));  // open: clr
  Register #(.width(32)) register_23 (.D(data_In), .en(decoder_1_out23), .Q(register_23_q), .clk(in_6));  // open: clr
  Register #(.width(32)) register_24 (.D(data_In), .en(decoder_1_out24), .Q(register_24_q), .clk(in_6));  // open: clr
  Register #(.width(32)) register_25 (.D(data_In), .en(decoder_1_out25), .Q(register_25_q), .clk(in_6));  // open: clr
  Register #(.width(32)) register_26 (.D(data_In), .en(decoder_1_out26), .Q(register_26_q), .clk(in_6));  // open: clr
  Register #(.width(32)) register_27 (.D(data_In), .en(decoder_1_out27), .Q(register_27_q), .clk(in_6));  // open: clr
  Register #(.width(32)) register_28 (.D(data_In), .en(decoder_1_out28), .Q(register_28_q), .clk(in_6));  // open: clr
  Register #(.width(32)) register_29 (.D(data_In), .en(decoder_1_out29), .Q(register_29_q), .clk(in_6));  // open: clr
  Register #(.width(32)) register_30 (.D(data_In), .en(decoder_1_out30), .Q(register_30_q), .clk(in_6));  // open: clr
  Register #(.width(32)) register_31 (.D(data_In), .en(decoder_1_out31), .Q(register_31_q), .clk(in_6));  // open: clr
  Multiplexer #(.select(5), .width(32), .enable("false")) multiplexer_1 (
    .in0({32{1'b0}}), .in1(register_1_q), .in2(register_2_q), .in3(register_3_q), .in4(register_4_q),
    .in5(register_5_q), .in6(register_6_q), .in7(register_7_q), .in8(register_8_q), .in9(register_9_q),
    .in10(register_10_q), .in11(register_11_q), .in12(register_12_q), .in13(register_13_q),
    .in14(register_14_q), .in15(register_15_q), .in16(register_16_q), .in17(register_17_q),
    .in18(register_18_q), .in19(register_19_q), .in20(register_20_q), .in21(register_21_q),
    .in22(register_22_q), .in23(register_23_q), .in24(register_24_q), .in25(register_25_q),
    .in26(register_26_q), .in27(register_27_q), .in28(register_28_q), .in29(register_29_q),
    .in30(register_30_q), .in31(register_31_q), .out(RS1), .sel(M1_selector));
  Multiplexer #(.select(5), .width(32), .enable("false")) multiplexer_2 (
    .in0({32{1'b0}}), .in1(register_1_q), .in2(register_2_q), .in3(register_3_q), .in4(register_4_q),
    .in5(register_5_q), .in6(register_6_q), .in7(register_7_q), .in8(register_8_q), .in9(register_9_q),
    .in10(register_10_q), .in11(register_11_q), .in12(register_12_q), .in13(register_13_q),
    .in14(register_14_q), .in15(register_15_q), .in16(register_16_q), .in17(register_17_q),
    .in18(register_18_q), .in19(register_19_q), .in20(register_20_q), .in21(register_21_q),
    .in22(register_22_q), .in23(register_23_q), .in24(register_24_q), .in25(register_25_q),
    .in26(register_26_q), .in27(register_27_q), .in28(register_28_q), .in29(register_29_q),
    .in30(register_30_q), .in31(register_31_q), .out(RS2), .sel(M2_selector));
endmodule

// control decode
module Control_Decode (
  input  R_Type,
  input  I_Type,
  input  Load,
  input  JALR,
  input  Store,
  input  Branch,
  input  Auipc,
  input  Lui,
  input  JAL,
  input  [2:0] func_3,
  input  fun_7,
  output REG_Write,
  output Branch_2,
  output Store_2,
  output Mem_2_Reg,
  output [1:0] Operand_A,
  output operang_B,
  output [1:0] IMM_SELECTOR,
  output [1:0] NEXT_PC,
  output [2:0] ALU,
  output [3:0] out_21
);

  wire or_1_out, or_2_out, or_3_out, or_4_out, or_5_out;

  or or_1 (or_1_out, JALR, Load, I_Type);
  or or_2 (or_2_out, R_Type, or_1_out, Store, Branch);
  or or_3 (or_3_out, Auipc, Lui);
  or or_4 (or_4_out, JAL, JALR);
  or or_5 (or_5_out, Lui, Auipc);
  or or_6 (REG_Write, I_Type, Load, JALR, R_Type, Auipc, Lui, JAL);
  operand operand_1 (
    .JAL_JALR(or_4_out), .AUIPC(Auipc), .ZERO(1'b0), .RS1(or_2_out), .output_0(Operand_A[1]),
    .output_1(Operand_A[0]));
  or or_7 (operang_B, or_5_out, Branch, I_Type, Store);
  IMM imm_1 (.IType(I_Type), .STYPE(Store), .UTYPE(or_3_out), .a(IMM_SELECTOR[1]), .b(IMM_SELECTOR[0]));
  NEXT_PC_SELECT next_pc_select_1 (.SBTYPE(Branch), .JALR(JALR), .JAL(JAL), .a(NEXT_PC[1]), .b(NEXT_PC[0]));
  ALU alu_1 (
    .RTYPE(R_Type), .ITYPE(I_Type), .LOAD(Load), .JALR(JALR), .STORE(Store), .AUIPC(Auipc), .LUI(Lui),
    .JAL(JAL), .OUT0(ALU[2]), .OUT1(ALU[1]), .OUT2(ALU[0]));
  alu_controller__AC alu_controller_ac_1 (
    .opcode_0(ALU[2]), .opcode_1(ALU[1]), .opcode_3(ALU[0]), .fun_3_0(func_3[2]), .fun_3_1(func_3[1]),
    .fun_3_2(func_3[0]), .func_7(fun_7), .output_0(out_21[3]), .output_1(out_21[2]), .output_2(out_21[1]),
    .output_3(out_21[0]));

  assign Branch_2 = Branch;
  assign Mem_2_Reg = Load;
  assign Store_2 = Store;
endmodule

module opereng_A__select (
  input  jal,
  input  jalr,
  input  auipc,
  output a,
  output b
);

  or or_1 (b, jalr, jal);

  assign a = auipc;
endmodule

module IMM (
  input  IType,
  input  STYPE,
  input  UTYPE,
  output a,
  output b
);

  wire not_1_out, not_2_out, not_3_out, not_4_out;

  not not_1 (not_1_out, IType);
  not not_2 (not_2_out, STYPE);
  not not_3 (not_3_out, IType);
  not not_4 (not_4_out, UTYPE);
  and and_1 (a, not_1_out, not_2_out);
  and and_2 (b, not_3_out, not_4_out);
endmodule

module NEXT_PC_SELECT (
  input  SBTYPE,
  input  JALR,
  input  JAL,
  output a,
  output b
);

  or or_1 (a, JALR, SBTYPE);
  or or_2 (b, JAL, SBTYPE);
endmodule

module CONTROL (
  input  [6:0] opcode_7_bit,
  input  [2:0] fun_3_bit,
  input  fun_7_bit,
  output reg_write,
  output branch,
  output store,
  output mem_2_reg,
  output [1:0] op_a_selector,
  output op_b_selector,
  output [1:0] imm_selector,
  output [1:0] next_pc,
  output [2:0] alu,
  output [3:0] selector
);

  wire decoder_1_i, decoder_1_i__jalr, decoder_1_i__load, decoder_1_r, decoder_1_s, decoder_1_sb,
       decoder_1_u__auipc, decoder_1_u__lui, decoder_1_uj__jal;

  decoder decoder_1 (
    .R(decoder_1_r), .I(decoder_1_i), .I__LOAD(decoder_1_i__load), .I__JALR(decoder_1_i__jalr),
    .S(decoder_1_s), .SB(decoder_1_sb), .U__AUIPC(decoder_1_u__auipc), .U__LUI(decoder_1_u__lui),
    .UJ__JAL(decoder_1_uj__jal), .in_1(opcode_7_bit));
  // Control_Decode control_decode_1: pin names not known; wires that end beside it: decoder_1_r, decoder_1_i, decoder_1_i__load, decoder_1_i__jalr, decoder_1_s, decoder_1_sb, decoder_1_u__auipc, decoder_1_u__lui, decoder_1_uj__jal, fun_3_bit, fun_7_bit, reg_write, branch, store, mem_2_reg, op_a_selector, op_b_selector, imm_selector, next_pc, alu, selector
endmodule

module ALU (
  input  RTYPE,
  input  ITYPE,
  input  LOAD,
  input  JALR,
  input  STORE,
  input  AUIPC,
  input  LUI,
  input  JAL,
  output OUT0,
  output OUT1,
  output OUT2
);

  wire or_1_out, or_2_out, or_3_out, or_4_out, or_5_out, or_6_out;

  or or_1 (or_1_out, JAL, LUI);
  or or_2 (or_2_out, AUIPC, STORE);
  or or_3 (or_3_out, JAL, LUI);
  or or_4 (or_4_out, JALR, LOAD);
  or or_5 (or_5_out, JAL, AUIPC);
  or or_6 (or_6_out, JALR, ITYPE);
  or or_7 (OUT0, or_1_out, or_2_out);
  or or_8 (OUT1, or_3_out, or_4_out);
  or or_9 (OUT2, or_5_out, or_6_out);
endmodule

module CONTROL_ALU (
  input  opcode_1,
  input  opcode_2,
  input  opcode_3,
  input  func_3_1,
  input  func_3_2,
  input  func_3_3,
  input  func_7_30,
  output ALU_SEL_0,
  output ALU_SEL_1,
  output ALU_SEL_2,
  output ALU_SEL_3
);

  wire and_1_out, and_2_out, and_3_out, and_4_out, and_5_out, and_6_out, and_7_out, and_8_out, and_9_out,
       and_10_out, and_11_out, and_12_out, and_13_out, and_14_out, and_15_out, and_16_out, and_17_out,
       and_18_out, and_19_out, and_20_out, and_21_out, and_22_out, and_23_out, and_24_out, and_25_out,
       and_26_out, and_27_out, and_28_out, and_29_out, and_30_out, and_31_out, and_32_out, and_33_out,
       and_34_out, and_35_out, and_36_out, and_37_out, and_38_out, and_39_out, and_40_out, and_41_out,
       and_42_out, and_43_out, and_44_out, and_45_out, and_46_out, and_47_out, not_1_out, not_2_out,
       not_3_out, not_4_out, not_5_out, not_6_out, not_7_out, not_8_out, not_9_out, not_10_out, not_11_out,
       not_12_out, not_13_out, not_14_out, not_15_out, not_16_out, not_17_out, not_18_out, not_19_out,
       not_20_out, not_21_out, not_22_out, not_23_out, not_24_out, not_25_out, not_26_out, not_27_out,
       not_28_out, not_29_out, not_30_out, not_31_out, not_32_out, not_33_out, not_34_out, not_35_out,
       not_36_out, or_1_out, or_2_out, or_3_out, or_4_out, or_5_out, or_6_out, or_7_out, or_8_out, or_10_out,
       or_11_out, or_12_out, or_13_out, or_14_out, or_15_out;

  not not_1 (not_1_out, opcode_2);
  not not_2 (not_2_out, func_3_1);
  not not_3 (not_3_out, opcode_3);
  not not_4 (not_4_out, func_3_2);
  not not_5 (not_5_out, opcode_1);
  not not_6 (not_6_out, func_3_1);
  not not_7 (not_7_out, opcode_1);
  not not_8 (not_8_out, opcode_2);
  not not_9 (not_9_out, func_3_2);
  not not_10 (not_10_out, func_3_3);
  not not_11 (not_11_out, opcode_2);
  not not_12 (not_12_out, func_3_2);
  not not_13 (not_13_out, func_7_30);
  not not_14 (not_14_out, opcode_2);
  not not_15 (not_15_out, opcode_3);
  not not_16 (not_16_out, func_3_1);
  not not_17 (not_17_out, opcode_2);
  not not_18 (not_18_out, opcode_3);
  not not_19 (not_19_out, func_3_1);
  not not_20 (not_20_out, opcode_1);
  not not_21 (not_21_out, func_3_1);
  not not_22 (not_22_out, opcode_1);
  and and_1 (and_1_out, not_1_out, func_3_1);
  not not_23 (not_23_out, func_3_2);
  and and_2 (and_2_out, opcode_2, not_2_out);
  not not_24 (not_24_out, func_7_30);
  and and_3 (and_3_out, not_3_out, not_4_out);
  and and_4 (and_4_out, not_5_out, not_6_out);
  and and_5 (and_5_out, not_7_out, func_3_3);
  and and_6 (and_6_out, not_8_out, not_9_out);
  and and_7 (and_7_out, not_10_out, func_7_30);
  and and_8 (and_8_out, not_11_out, func_3_1);
  and and_9 (and_9_out, not_12_out, not_13_out);
  not not_25 (not_25_out, opcode_3);
  not not_26 (not_26_out, opcode_2);
  and and_10 (and_10_out, not_14_out, not_15_out);
  and and_11 (and_11_out, not_16_out, func_7_30);
  and and_12 (and_12_out, not_17_out, func_3_2);
  not not_27 (not_27_out, opcode_2);
  not not_28 (not_28_out, func_3_2);
  not not_29 (not_29_out, func_3_3);
  and and_13 (and_13_out, opcode_3, func_3_1);
  not not_30 (not_30_out, func_3_3);
  not not_31 (not_31_out, opcode_1);
  and and_14 (and_14_out, not_18_out, not_19_out);
  and and_15 (and_15_out, not_20_out, not_21_out);
  and and_16 (and_16_out, not_22_out, func_3_1);
  not not_32 (not_32_out, func_3_2);
  and and_17 (and_17_out, and_1_out, not_23_out);
  and and_18 (and_18_out, func_3_3, func_7_30);
  not not_33 (not_33_out, opcode_3);
  and and_19 (and_19_out, and_2_out, func_3_2);
  and and_20 (and_20_out, func_3_3, not_24_out);
  and and_21 (and_21_out, and_3_out, func_7_30);
  and and_22 (and_22_out, and_4_out, func_3_3);
  and and_23 (and_23_out, and_5_out, func_7_30);
  and and_24 (and_24_out, opcode_1, opcode_2);
  and and_25 (and_25_out, and_6_out, and_7_out);
  and and_26 (and_26_out, and_8_out, and_9_out);
  and and_27 (and_27_out, not_25_out, func_3_1);
  not not_34 (not_34_out, func_3_3);
  and and_28 (and_28_out, opcode_1, not_26_out);
  and and_29 (and_29_out, opcode_1, opcode_2);
  not not_35 (not_35_out, opcode_3);
  and and_30 (and_30_out, and_10_out, and_11_out);
  and and_31 (and_31_out, and_12_out, func_3_3);
  and and_32 (and_32_out, not_27_out, func_3_1);
  and and_33 (and_33_out, not_28_out, not_29_out);
  and and_34 (and_34_out, and_13_out, not_30_out);
  and and_35 (and_35_out, not_31_out, opcode_2);
  and and_36 (and_36_out, and_14_out, func_7_30);
  and and_37 (and_37_out, and_15_out, func_3_2);
  and and_38 (and_38_out, and_16_out, not_32_out);
  and and_39 (and_39_out, and_17_out, and_18_out);
  and and_40 (and_40_out, opcode_2, not_33_out);
  and and_41 (and_41_out, and_19_out, and_20_out);
  not not_36 (not_36_out, opcode_3);
  or or_1 (or_1_out, and_21_out, and_22_out);
  or or_2 (or_2_out, and_23_out, and_24_out);
  or or_3 (or_3_out, and_25_out, and_26_out);
  and and_42 (and_42_out, and_27_out, not_34_out);
  and and_43 (and_43_out, and_28_out, opcode_3);
  and and_44 (and_44_out, and_29_out, not_35_out);
  or or_4 (or_4_out, and_30_out, and_31_out);
  and and_45 (and_45_out, and_32_out, and_33_out);
  or or_5 (or_5_out, and_34_out, and_35_out);
  and and_46 (and_46_out, opcode_1, opcode_3);
  or or_6 (or_6_out, and_36_out, and_37_out);
  or or_7 (or_7_out, and_38_out, and_39_out);
  or or_8 (or_8_out, and_40_out, and_41_out);
  and and_47 (and_47_out, opcode_1, not_36_out);
  or or_9 (ALU_SEL_1, or_1_out, or_2_out);
  or or_10 (or_10_out, or_3_out, and_42_out);
  or or_11 (or_11_out, and_43_out, and_44_out);
  or or_12 (or_12_out, or_4_out, and_45_out);
  or or_13 (or_13_out, or_5_out, and_46_out);
  or or_14 (or_14_out, or_6_out, or_7_out);
  or or_15 (or_15_out, or_8_out, and_47_out);
  or or_16 (ALU_SEL_2, or_10_out, or_11_out);
  or or_17 (ALU_SEL_3, or_12_out, or_13_out);
  or or_18 (ALU_SEL_0, or_14_out, or_15_out);
endmodule

module ALU_CONTROLLER_CORRECT (
  input  opcode_0,
  input  opcode_1,
  input  opcode_2,
  input  func_3_0,
  input  func_3_1,
  input  func_3_2,
  input  func_7,
  output output_0,
  output output_1,
  output output_2,
  output output_3
);

  wire and_1_out, and_2_out, and_3_out, and_4_out, and_5_out, and_6_out, and_7_out, and_8_out, and_9_out,
       and_10_out, and_11_out, and_12_out, and_13_out, and_14_out, and_15_out, and_16_out, and_17_out,
       and_18_out, and_19_out, and_20_out, and_21_out, and_22_out, and_23_out, and_24_out, and_25_out,
       and_26_out, and_27_out, and_28_out, and_29_out, and_30_out, and_31_out, not_1_out, not_2_out,
       not_3_out, not_4_out, not_5_out, not_6_out, not_7_out, not_8_out, not_9_out, not_10_out, not_11_out,
       not_12_out, not_13_out, not_14_out, not_15_out, not_16_out, not_17_out, not_18_out, not_19_out,
       not_20_out, not_21_out, not_22_out, not_23_out, not_24_out, not_25_out, or_1_out, or_2_out, or_3_out,
       or_4_out, or_7_out, or_8_out;

  not not_1 (not_1_out, opcode_0);
  not not_2 (not_2_out, opcode_1);
  not not_3 (not_3_out, func_3_0);
  not not_4 (not_4_out, opcode_0);
  not not_5 (not_5_out, opcode_0);
  not not_6 (not_6_out, opcode_2);
  not not_7 (not_7_out, func_3_1);
  not not_8 (not_8_out, opcode_0);
  not not_9 (not_9_out, func_3_0);
  not not_10 (not_10_out, opcode_0);
  not not_11 (not_11_out, func_3_1);
  not not_12 (not_12_out, opcode_0);
  not not_13 (not_13_out, opcode_2);
  not not_14 (not_14_out, opcode_0);
  not not_15 (not_15_out, opcode_0);
  not not_16 (not_16_out, func_3_1);
  not not_17 (not_17_out, func_3_2);
  and and_1 (and_1_out, not_1_out, not_2_out);
  and and_2 (and_2_out, not_3_out, func_3_1);
  and and_3 (and_3_out, not_4_out, func_3_0);
  not not_18 (not_18_out, func_3_1);
  and and_4 (and_4_out, not_5_out, not_6_out);
  and and_5 (and_5_out, not_7_out, func_7);
  and and_6 (and_6_out, not_8_out, not_9_out);
  and and_7 (and_7_out, not_10_out, not_11_out);
  and and_8 (and_8_out, func_3_2, func_7);
  and and_9 (and_9_out, not_12_out, not_13_out);
  not not_19 (not_19_out, func_3_0);
  not not_20 (not_20_out, func_3_1);
  not not_21 (not_21_out, opcode_0);
  not not_22 (not_22_out, func_3_1);
  not not_23 (not_23_out, func_7);
  not not_24 (not_24_out, opcode_0);
  and and_10 (and_10_out, not_14_out, func_3_1);
  and and_11 (and_11_out, not_15_out, func_3_0);
  and and_12 (and_12_out, not_16_out, not_17_out);
  and and_13 (and_13_out, and_1_out, and_2_out);
  and and_14 (and_14_out, and_3_out, not_18_out);
  and and_15 (and_15_out, and_4_out, and_5_out);
  and and_16 (and_16_out, and_6_out, func_3_2);
  and and_17 (and_17_out, and_7_out, and_8_out);
  and and_18 (and_18_out, opcode_1, opcode_2);
  and and_19 (and_19_out, and_9_out, not_19_out);
  and and_20 (and_20_out, not_20_out, func_7);
  and and_21 (and_21_out, not_21_out, func_3_0);
  and and_22 (and_22_out, not_22_out, not_23_out);
  and and_23 (and_23_out, not_24_out, func_3_0);
  not not_25 (not_25_out, func_3_2);
  and and_24 (and_24_out, and_10_out, func_3_2);
  and and_25 (and_25_out, and_11_out, and_12_out);
  or or_1 (or_1_out, and_13_out, and_14_out);
  and and_26 (and_26_out, opcode_1, opcode_2);
  or or_2 (or_2_out, and_15_out, and_16_out);
  or or_3 (or_3_out, and_17_out, and_18_out);
  and and_27 (and_27_out, and_19_out, and_20_out);
  and and_28 (and_28_out, and_21_out, and_22_out);
  and and_29 (and_29_out, and_23_out, not_25_out);
  and and_30 (and_30_out, opcode_1, opcode_2);
  or or_4 (or_4_out, and_24_out, and_25_out);
  and and_31 (and_31_out, opcode_1, opcode_2);
  or or_5 (output_0, or_1_out, and_26_out);
  or or_6 (output_1, or_2_out, or_3_out);
  or or_7 (or_7_out, and_27_out, and_28_out);
  or or_8 (or_8_out, and_29_out, and_30_out);
  or or_9 (output_3, or_4_out, and_31_out);
  or or_10 (output_2, or_7_out, or_8_out);
endmodule

module operand_A_select (
  input  JAL_JALR,
  input  AUIPC,
  input  ZERO,
  input  RS1,
  output output_0,
  output output_1
);

  wire not_1_out, not_2_out, not_3_out, not_4_out;

  not not_1 (not_1_out, JAL_JALR);
  and and_1 (output_0, not_1_out, not_2_out);
  not not_2 (not_2_out, RS1);
  not not_3 (not_3_out, AUIPC);
  and and_2 (output_1, not_3_out, not_4_out);
  not not_4 (not_4_out, RS1);
endmodule

module alu_main (
  input  [31:0] in_1,
  input  [31:0] in_2,
  input  [3:0] in_3,
  output [31:0] out_4
);

  wire comparator_1_lt, comparator_2_lt;
  wire [31:0] adder_1_out, and_1_out, bit_extender_1_out, bit_extender_2_out, or_1_out, shifter_1_out,
       shifter_2_out, shifter_3_out, subtractor_1_out, xor_1_out;

  Adder #(.width(32)) adder_1 (.a(in_1), .b(in_2), .out(adder_1_out));  // open: cin, cout
  Subtractor #(.width(32)) subtractor_1 (.a(in_1), .b(in_2), .out(subtractor_1_out));  // open: bin, bout
  assign and_1_out = in_1 & in_2;  // AND_Gate and_1, 32 bits wide
  assign or_1_out = in_1 | in_2;  // OR_Gate or_1, 32 bits wide
  Shifter #(.width(32)) shifter_1 (.in(in_1), .\dist (in_2[4:0]), .out(shifter_1_out));
  Shifter #(.width(32), .shift("lr")) shifter_2 (.in(in_1), .\dist (in_2[4:0]), .out(shifter_2_out));
  Shifter #(.width(32), .shift("ar")) shifter_3 (.in(in_1), .\dist (in_2[4:0]), .out(shifter_3_out));
  Comparator #(.width(32)) comparator_1 (.a(in_1), .b(in_2), .lt(comparator_1_lt));  // open: gt, eq
  Comparator #(.width(32), .mode("unsigned")) comparator_2 (.a(in_1), .b(in_2), .lt(comparator_2_lt));  // open: gt, eq
  assign xor_1_out = in_1 ^ in_2;  // XOR_Gate xor_1, 32 bits wide
  assign bit_extender_1_out = {{31{1'b0}}, comparator_1_lt};  // Bit_Extender bit_extender_1
  assign bit_extender_2_out = {{31{1'b0}}, comparator_2_lt};  // Bit_Extender bit_extender_2
  Multiplexer #(.select(4), .width(32)) multiplexer_1 (
    .in0(adder_1_out), .in1(and_1_out), .in2(or_1_out), .in3(bit_extender_2_out), .in4(shifter_1_out),
    .in6(subtractor_1_out), .in8(bit_extender_1_out), .in10(shifter_2_out), .in11(xor_1_out),
    .in12(shifter_3_out), .in15(in_1), .out(out_4), .sel(in_3));  // open: in5, in7, in9, in13, in14, en
endmodule

module alu_controller__AC (
  input  opcode_0,
  input  opcode_1,
  input  opcode_3,
  input  fun_3_0,
  input  fun_3_1,
  input  fun_3_2,
  input  func_7,
  output output_0,
  output output_1,
  output output_2,
  output output_3
);

  wire and_1_out, and_2_out, and_3_out, and_4_out, and_5_out, and_6_out, and_7_out, and_8_out, and_9_out,
       and_10_out, and_11_out, and_12_out, and_13_out, and_14_out, and_15_out, and_16_out, and_17_out,
       and_18_out, and_19_out, and_20_out, and_21_out, and_22_out, and_23_out, and_24_out, and_25_out,
       and_26_out, and_27_out, and_28_out, and_29_out, and_30_out, and_31_out, and_32_out, and_33_out,
       and_34_out, and_35_out, and_36_out, and_37_out, and_38_out, and_39_out, and_40_out, and_41_out,
       and_42_out, and_43_out, and_44_out, not_1_out, not_2_out, not_3_out, not_4_out, not_5_out, not_6_out,
       not_7_out, not_8_out, not_9_out, not_10_out, not_11_out, not_12_out, not_13_out, not_14_out,
       not_15_out, not_16_out, not_17_out, not_18_out, not_19_out, not_20_out, not_21_out, not_22_out,
       not_23_out, not_24_out, not_25_out, not_26_out, not_27_out, not_28_out, not_29_out, not_30_out,
       not_31_out, not_32_out, not_33_out, not_34_out, not_35_out, not_36_out, not_37_out, or_1_out,
       or_2_out, or_3_out, or_4_out, or_5_out, or_8_out, or_9_out;

  not not_1 (not_1_out, opcode_0);
  not not_2 (not_2_out, opcode_1);
  not not_3 (not_3_out, opcode_0);
  not not_4 (not_4_out, opcode_1);
  not not_5 (not_5_out, opcode_0);
  not not_6 (not_6_out, opcode_1);
  not not_7 (not_7_out, opcode_0);
  not not_8 (not_8_out, opcode_1);
  not not_9 (not_9_out, opcode_0);
  not not_10 (not_10_out, opcode_1);
  not not_11 (not_11_out, opcode_0);
  not not_12 (not_12_out, opcode_1);
  and and_1 (and_1_out, not_1_out, not_2_out);
  not not_13 (not_13_out, fun_3_0);
  not not_14 (not_14_out, fun_3_2);
  not not_15 (not_15_out, opcode_0);
  not not_16 (not_16_out, opcode_1);
  not not_17 (not_17_out, fun_3_1);
  not not_18 (not_18_out, opcode_0);
  not not_19 (not_19_out, opcode_1);
  not not_20 (not_20_out, opcode_3);
  and and_2 (and_2_out, not_3_out, not_4_out);
  not not_21 (not_21_out, fun_3_0);
  not not_22 (not_22_out, fun_3_1);
  and and_3 (and_3_out, not_5_out, not_6_out);
  not not_23 (not_23_out, fun_3_1);
  and and_4 (and_4_out, not_7_out, not_8_out);
  not not_24 (not_24_out, opcode_3);
  not not_25 (not_25_out, fun_3_0);
  and and_5 (and_5_out, not_9_out, not_10_out);
  not not_26 (not_26_out, fun_3_0);
  not not_27 (not_27_out, opcode_0);
  not not_28 (not_28_out, opcode_1);
  not not_29 (not_29_out, opcode_0);
  not not_30 (not_30_out, opcode_1);
  and and_6 (and_6_out, not_11_out, not_12_out);
  not not_31 (not_31_out, fun_3_1);
  not not_32 (not_32_out, fun_3_2);
  and and_7 (and_7_out, and_1_out, not_13_out);
  and and_8 (and_8_out, fun_3_1, not_14_out);
  and and_9 (and_9_out, not_15_out, not_16_out);
  and and_10 (and_10_out, fun_3_0, not_17_out);
  and and_11 (and_11_out, not_18_out, not_19_out);
  and and_12 (and_12_out, not_20_out, func_7);
  and and_13 (and_13_out, and_2_out, not_21_out);
  and and_14 (and_14_out, not_22_out, fun_3_2);
  and and_15 (and_15_out, and_3_out, not_23_out);
  and and_16 (and_16_out, fun_3_2, func_7);
  and and_17 (and_17_out, and_4_out, not_24_out);
  and and_18 (and_18_out, not_25_out, func_7);
  and and_19 (and_19_out, and_5_out, not_26_out);
  and and_20 (and_20_out, fun_3_1, fun_3_2);
  and and_21 (and_21_out, not_27_out, not_28_out);
  not not_33 (not_33_out, fun_3_1);
  not not_34 (not_34_out, func_7);
  not not_35 (not_35_out, opcode_0);
  not not_36 (not_36_out, opcode_1);
  not not_37 (not_37_out, fun_3_2);
  and and_22 (and_22_out, not_29_out, not_30_out);
  and and_23 (and_23_out, fun_3_1, fun_3_2);
  and and_24 (and_24_out, and_6_out, fun_3_0);
  and and_25 (and_25_out, not_31_out, not_32_out);
  and and_26 (and_26_out, and_7_out, and_8_out);
  and and_27 (and_27_out, and_9_out, and_10_out);
  and and_28 (and_28_out, and_11_out, and_12_out);
  and and_29 (and_29_out, and_13_out, and_14_out);
  and and_30 (and_30_out, and_15_out, and_16_out);
  and and_31 (and_31_out, opcode_1, opcode_3);
  and and_32 (and_32_out, and_17_out, and_18_out);
  and and_33 (and_33_out, and_19_out, and_20_out);
  and and_34 (and_34_out, and_21_out, fun_3_0);
  and and_35 (and_35_out, not_33_out, not_34_out);
  and and_36 (and_36_out, not_35_out, not_36_out);
  and and_37 (and_37_out, fun_3_0, not_37_out);
  and and_38 (and_38_out, and_22_out, and_23_out);
  and and_39 (and_39_out, and_24_out, and_25_out);
  or or_1 (or_1_out, and_26_out, and_27_out);
  and and_40 (and_40_out, opcode_1, opcode_3);
  or or_2 (or_2_out, and_28_out, and_29_out);
  or or_3 (or_3_out, and_30_out, and_31_out);
  or or_4 (or_4_out, and_32_out, and_33_out);
  and and_41 (and_41_out, and_34_out, and_35_out);
  and and_42 (and_42_out, and_36_out, and_37_out);
  and and_43 (and_43_out, opcode_1, opcode_3);
  or or_5 (or_5_out, and_38_out, and_39_out);
  and and_44 (and_44_out, opcode_1, opcode_3);
  or or_6 (output_0, or_1_out, and_40_out);
  or or_7 (output_1, or_2_out, or_3_out);
  or or_8 (or_8_out, or_4_out, and_41_out);
  or or_9 (or_9_out, and_42_out, and_43_out);
  or or_10 (output_3, or_5_out, and_44_out);
  or or_11 (output_2, or_8_out, or_9_out);
endmodule

module operandselect (
  input  JAL_JALR,
  input  AUIPC,
  input  ZERO,
  input  RS1,
  output output_0,
  output output_1
);

  wire and_2_out, and_3_out, and_4_out, and_5_out, not_1_out, not_2_out, not_3_out, not_4_out, not_5_out,
       not_6_out, not_7_out, not_8_out;

  not not_1 (not_1_out, JAL_JALR);
  and and_1 (output_0, not_1_out, not_2_out);
  not not_2 (not_2_out, RS1);
  not not_3 (not_3_out, JAL_JALR);
  and and_2 (and_2_out, not_3_out, not_4_out);
  not not_4 (not_4_out, AUIPC);
  not not_5 (not_5_out, RS1);
  not not_6 (not_6_out, AUIPC);
  and and_3 (and_3_out, not_6_out, not_7_out);
  not not_7 (not_7_out, ZERO);
  not not_8 (not_8_out, RS1);
  and and_4 (and_4_out, and_2_out, not_5_out);
  and and_5 (and_5_out, and_3_out, not_8_out);
  or or_1 (output_1, and_4_out, and_5_out);
endmodule

module BRANCH (
  input  [31:0] RS_1,
  input  [31:0] RS_2,
  input  [2:0] selector,
  output \output 
);

  wire comparator_1_eq, comparator_2_eq, comparator_3_eq, comparator_4_eq, comparator_4_gt, comparator_5_lt,
       comparator_6_eq, comparator_6_gt, not_1_out, or_1_out, or_2_out, undriven;

  Comparator #(.width(32)) comparator_1 (.a(RS_1), .b(RS_2), .eq(comparator_1_eq));  // open: gt, lt
  not not_1 (not_1_out, comparator_2_eq);
  Comparator #(.width(32)) comparator_2 (.a(RS_1), .b(RS_2), .eq(comparator_2_eq));  // open: gt, lt
  Comparator #(.width(32)) comparator_3 (.a(RS_1), .b(RS_2), .eq(comparator_3_eq));  // open: gt, lt
  Comparator #(.width(32)) comparator_4 (.a(RS_1), .b(RS_2), .gt(comparator_4_gt), .eq(comparator_4_eq));  // open: lt
  or or_1 (or_1_out, comparator_4_gt, comparator_4_eq);
  Comparator #(.width(32), .mode("unsigned")) comparator_5 (.a(RS_1), .b(RS_2), .lt(comparator_5_lt));  // open: gt, eq
  Comparator #(.width(32), .mode("unsigned")) comparator_6 (
    .a(RS_1), .b(RS_2), .gt(comparator_6_gt), .eq(comparator_6_eq));  // open: lt
  or or_2 (or_2_out, comparator_6_gt, comparator_6_eq);
  Multiplexer #(.select(3)) multiplexer_1 (
    .in0(comparator_1_eq), .in1(not_1_out), .in4(comparator_3_eq), .in5(or_1_out), .in6(comparator_5_lt),
    .in7(or_2_out), .out(\output ), .sel(selector), .en(undriven));  // open: in2, in3
endmodule

module operand (
  input  JAL_JALR,
  input  AUIPC,
  input  ZERO,
  input  RS1,
  output output_0,
  output output_1
);

  or or_1 (output_0, ZERO, AUIPC);
  or or_2 (output_1, ZERO, JAL_JALR);
endmodule
